# Fritzing sketch Composite PCB (saved by Fritzing 0.9.4)
circuit board: 8.94804cm x 5.63607cm

parts:
  R2 = Resistor [tolerance=±5% resistance=10k package=THT]
  R3 = Resistor [tolerance=±5% resistance=470 package=THT]
  R4 = Resistor [tolerance=±5% resistance=180 package=THT]
  R5 = Resistor [tolerance=±5% resistance=680 package=THT]
  R6 = Resistor [tolerance=±5% resistance=330 package=THT]
  R8 = Resistor [tolerance=±5% resistance=47k package=THT]
  R10 = Resistor [tolerance=±5% resistance=22k package=THT]
  R13 = Resistor [tolerance=±5% resistance=680k package=THT]
  R15 = Resistor [tolerance=±5% resistance=22k package=THT]
  R16 = Resistor [tolerance=±5% resistance=33k package=THT]
  R17 = Resistor [tolerance=±5% resistance=3.3k package=THT]
  Q4 = Basic FET P-Channel [part_number=12v package="TO220 [THT]"]
  J3 = female pin header, 8 pins [form="♀ (female)"]
  J2 = female pin header, 1 pin [form="♀ (female)"]
  C3 = Tantalum Capacitor [capacitance=100nF voltage=16V package="100 mil [THT, tantalum]"]
  C4 = Tantalum Capacitor [capacitance=22nF voltage=16V package="100 mil [THT, tantalum]"]
  C7 = Tantalum Capacitor [capacitance=100nF voltage=16V package="100 mil [THT, tantalum]"]
  R11 = Resistor [tolerance=±5% resistance=1k package=THT]
  R12 = Resistor [tolerance=±5% resistance=1k package=THT]
  R7 = Resistor [tolerance=±5% resistance=4.7k package=THT]
  R9 = Resistor [tolerance=±5% resistance=330k package=THT]
  C6 = Tantalum Capacitor [capacitance=220nF voltage=16V package="100 mil [THT, tantalum]"]
  Q1 = NPN-Transistor [package="TO92 [THT]"]
  C1 = Electrolytic Capacitor [capacitance=470µF voltage=16V package="100 mil [THT, electrolytic]"]
  R1 = Resistor [tolerance=±5% resistance=10k package=THT]
  Q3 = PNP-Transistor [package="TO92 [THT]"]
  R14 = Resistor [tolerance=±5% resistance=10k package=THT]
  D1 = Rectifier Diode [part_number=1N4001 package="300 mil [THT]"]
  D2 = Rectifier Diode [part_number=1N4001 package="300 mil [THT]"]
  C5 = Electrolytic Capacitor [capacitance=100µF voltage=16V package="100 mil [THT, electrolytic]"]
  C2 = Electrolytic Capacitor [capacitance=47µF voltage=16V package="100 mil [THT, electrolytic]"]
  Q2 = NPN-Transistor [package="TO92 [THT]"]
  IC2 = DIP - 8 pins [chip_label=IC package="DIP (Dual Inline) [THT]"]
  RCA1 = prefix0000

nets:
  N1: R2.Pin_0, R3.Pin_1, R5.Pin_1, R10.Pin_0, R13.Pin_1, Q4.drain, J3.pin2, C3.-, C4.-, R11.Pin_1, C1.-, C5.-, IC2.Ground, RCA1.connector1
  N2: R2.Pin_1, R1.Pin_0, C2.+, Q2.B
  N3: R3.Pin_0, R4.Pin_1, Q2.C
  N4: R4.Pin_0, Q1.B
  N5: R5.Pin_0, R6.Pin_0, Q1.C, Q3.E
  N6: R6.Pin_1, C5.+
  N7: R8.Pin_0, J3.pin8, R7.Pin_0
  N8: R8.Pin_1, R17.Pin_0
  N9: R10.Pin_1, R17.Pin_1, R9.Pin_1
  N10: R13.Pin_0, C3.+, IC2.RSet
  N11: R15.Pin_0, R16.Pin_0, Q3.B, R14.Pin_1
  N12: R15.Pin_1, C4.+, D1.anode
  N13: R16.Pin_1, D2.anode
  N14: Q4.gate, J3.pin4
  N15: Q4.source, C1.+, R1.Pin_1, Q3.C, R14.Pin_0, Q2.E, IC2.VCC
  N16: J3.pin5, R11.Pin_0, R12.Pin_0
  N17: J2.pin1, R9.Pin_0, C6.-
  N18: C7.-, C2.-, RCA1.connector0
  N19: C7.+, IC2.Video_In
  N20: R12.Pin_1, D2.cathode, IC2.Sync_Out
  N21: R7.Pin_1, C6.+, Q1.E
  N22: D1.cathode, IC2.VSync_Out

notes:
  Composite Minitel
  Clément MOINE . 17.04.20 . v1.0.0

custom parts:
  DIP - 8 pins: A DIP stand-in part for whatever IC you want. With 8 pins on a 300mil dual inline package (DIP) footprint.
