# Fritzing sketch Preamplificateur Composite PCB (saved by Fritzing 0.9.4)
circuit board: 8.46667cm x 5.90355cm
breadboards: 1

parts:
  R6 = Resistor [tolerance=±5% resistance=330 package=THT]
  D2 = Zener Diode [part_number=1N4740A breakdown_voltage=7.6V package="300 mil [THT]"]
  R8 = TRIMPOT [part_number=2.2kΩ package=3362u-2]
  C2 = Tantalum Capacitor [capacitance=100nF package="100 mil [THT, tantalum]"]
  R4 = Resistor [tolerance=±5% resistance=4.7k package=THT]
  D1 = Rectifier Diode [part_number=1N4001 package="300 mil [THT]"]
  J1 = female pin header, 2 pins [form="♀ (female)"]
  J2 = female pin header, 2 pins [form="♀ (female)"]
  R3 = Resistor [tolerance=±5% resistance=4.7k package=THT]
  R7 = TRIMPOT [part_number=22kΩ package=3362u-2]
  C1 = Tantalum Capacitor [capacitance=100nF package="100 mil [THT, tantalum]"]
  Q1 = NPN-Transistor [part_number=2N3904 package="TO92 [THT]"]
  Q2 = PNP-Transistor [part_number=2N2907 package="TO92 [THT]"]
  R5 = Resistor [tolerance=±5% resistance=68 package=THT]
  J3 = female pin header, 2 pins [form="♀ (female)"]
  R2 = Resistor [tolerance=±5% resistance=2.2k package=THT]
  C3 = Electrolytic Capacitor [capacitance=150µF package="100 mil [THT, electrolytic]"]
  R1 = Resistor [tolerance=±5% resistance=150 package=THT]
  C4 = Electrolytic Capacitor [capacitance=150µF package="100 mil [THT, electrolytic]"]

nets:
  N1: R6.Pin_0, D1.cathode, C4.+
  N2: R6.Pin_1, D2.cathode, C2.+, R4.Pin_0, R7.WIPER, Q2.E
  N3: D2.anode, R8.CW, C2.-, J1.pin1, J2.pin2, C1.+, J3.pin1, R2.Pin_0, R1.Pin_1, C4.-
  N4: R8.CCW, Q2.C, R5.Pin_1
  N5: R8.WIPER, Q1.C
  N6: R4.Pin_1, Q1.E, Q2.B
  N7: D1.anode, J1.pin2
  N8: J2.pin1, C3.-, R1.Pin_0
  N9: R3.Pin_0, R7.CCW
  N10: R3.Pin_1, Q1.B, R2.Pin_1, C3.+
  N11: R7.CW, C1.-
  N12: R5.Pin_0, J3.pin2
